// Digital circuit circuit.dig as structural Verilog
module circuit (
  input  in_1,
  input  in_2,
  input  SCLR,
  input  DS,
  input  STCP,
  input  SHCP,
  input  in_13,
  input  in_14,
  input  in_15,
  input  in_16,
  output out_3,
  output out_4,
  output QA,
  output QB,
  output QC,
  output QD
);

  wire jk_ff_as_1_nq, jk_ff_as_1_q, jk_ff_as_2_nq, jk_ff_as_2_q, jk_ff_as_3_nq, jk_ff_as_3_q, jk_ff_as_4_q,
       not_1_out, not_2_out;

  not not_1 (not_1_out, DS);
  not not_2 (not_2_out, in_1);
  JK_FF_AS jk_ff_as_1 (.Set(in_13), .J(DS), .C(SHCP), .K(not_1_out), .Clr(SCLR), .Q(jk_ff_as_1_q), .nQ(jk_ff_as_1_nq));
  RS_FF rs_ff_1 (.S(in_1), .C(in_2), .R(not_2_out), .Q(out_3), .nQ(out_4));
  and and_1 (QA, STCP, jk_ff_as_1_q);
  JK_FF_AS jk_ff_as_2 (
    .Set(in_14), .J(jk_ff_as_1_q), .C(SHCP), .K(jk_ff_as_1_nq), .Clr(SCLR), .Q(jk_ff_as_2_q),
    .nQ(jk_ff_as_2_nq));
  and and_2 (QB, STCP, jk_ff_as_2_q);
  JK_FF_AS jk_ff_as_3 (
    .Set(in_15), .J(jk_ff_as_2_q), .C(SHCP), .K(jk_ff_as_2_nq), .Clr(SCLR), .Q(jk_ff_as_3_q),
    .nQ(jk_ff_as_3_nq));
  and and_3 (QC, STCP, jk_ff_as_3_q);
  JK_FF_AS jk_ff_as_4 (
    .Set(in_16), .J(jk_ff_as_3_q), .C(SHCP), .K(jk_ff_as_3_nq), .Clr(SCLR), .Q(jk_ff_as_4_q));  // open: nQ
  and and_4 (QD, STCP, jk_ff_as_4_q);
endmodule
